# Fritzing sketch sensor station (saved by Fritzing 1.0.6)

parts:
  DHT1 = DHT11 Humitidy and Temperature Sensor (3 pins)
  Part1 = GY-BMEP280 Barometric Pressure Sensor - Breakout
  U1 = LuaNode32 / ESP32 [part_number=ESP32S-PIN30]

nets:
  N1: DHT1.Plus, Part1.SDO, U1.3V3
  N2: DHT1.Signal, U1.D15
  GND: DHT1.Gnd, Part1.CSB, U1.GND
  N3: Part1.SCL, U1.RX0
  N4: Part1.SDA, U1.D22

custom parts:
  DHT11 Humitidy and Temperature Sensor (3 pins): DHT11 Humidity and Temperature Sensor (3 pins).
  GY-BMEP280 Barometric Pressure Sensor - Breakout: The BME280 is a chip which was originally designed for the next generation of smartphones. It is made up of a very accurate pressure sensor and an associated temperature sensor which helps calibrate the pressure readings. And just for fun they threw in a pretty solid humidity sensor in there as well! So with an I2C connection you have access to enough weather data to make some pretty good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
  LuaNode32 / ESP32: New Image for LuaNode32 DOIT ESP32 DEVKIT V1. Base parts from LuaNode32 / ESP32 ESP32 based LuaNode32 by G.Noorlander DOIT Esp32 DevKit v1 (30 pins long, 11 pins width) by Werner Rothschopf (modified by vanepp Dec 2018)
